// Logisim project ALU.circ as structural Verilog: 28 circuits, main circuit ALU_demo
module ALU_demo (
  input  [28:0] in_1,
  input  [28:0] in_2
);

  wire operate_out, sw_1_y, takeInput_p1;
  wire [1:0] enc2_1_enc;
  wire [3:0] dipswitch_1_p1;
  wire [28:0] AX, BX, multpx_1_y, multpx_2_y, Result;

  // Switch takeInput: pin names not known; wires that end beside it: takeInput_p1
  sw sw_1 (.S(takeInput_p1), .Y(sw_1_y));
  one one_1 ();  // open: out_1
  Button operate (.out(operate_out));
  // DipSwitch #(.number(4)) dipswitch_1: pin names not known; wires that end beside it: dipswitch_1_p1, AX
  enc2 enc2_1 (.enc(enc2_1_enc));  // open: i0, i1, i3, i2
  multpx multpx_1 (.i0(Result), .i1(in_1), .S(sw_1_y), .Y(multpx_1_y));
  reg29f reg29f_1 (.D(multpx_2_y), .clk(operate_out), .Q(BX));
  reg29 reg29_1 (.D(multpx_1_y), .clk(operate_out), .Q(AX));
  // ALU alu_1: pin names not known; wires that end beside it: AX, enc2_1_enc, Result, BX, dipswitch_1_p1
  multpx multpx_2 (.i0(BX), .i1(in_2), .S(sw_1_y), .Y(multpx_2_y));
  reg4 reg4_1 (.d(dipswitch_1_p1), .en(sw_1_y), .c(operate_out));  // open: q
  // Probe on AX
  // Probe on AX
  // Probe on BX
  // Probe on BX
endmodule

module CLA4_Adder (
  input  [3:0] A,
  input  [3:0] B,
  input  Cin,
  output G,
  output P,
  output C,
  output [3:0] S
);

  wire [3:0] and4_1_nd, cla4_1_c0, xor4_1_x;

  // Probe on A
  XOR4 xor4_1 (.B(B), .A(A), .x(xor4_1_x));
  AND4 and4_1 (.A(A), .B(B), .nd(and4_1_nd));
  // Probe on B
  pgen pgen_1 (.pi(xor4_1_x), .p(P));
  gGen ggen_1 (.pi(xor4_1_x), .gi(and4_1_nd), .g(G));
  CLA4 cla4_1 (
    .G2(and4_1_nd[2]), .G3(and4_1_nd[3]), .G0(and4_1_nd[0]), .G1(and4_1_nd[1]), .P2(xor4_1_x[2]),
    .P3(xor4_1_x[3]), .Cin(Cin), .P0(xor4_1_x[0]), .P1(xor4_1_x[1]), .C1(cla4_1_c0[1]), .C2(cla4_1_c0[2]),
    .C3(cla4_1_c0[3]), .C4(C), .C0(cla4_1_c0[0]));
  XOR4 xor4_2 (.B(xor4_1_x), .A(cla4_1_c0), .x(S));
  // Probe on S
endmodule

module CLA4 (
  input  P0,
  input  G0,
  input  P1,
  input  G1,
  input  P2,
  input  G2,
  input  P3,
  input  G3,
  input  Cin,
  output C0,
  output C1,
  output C2,
  output C3,
  output C4
);

  wire and_1_out, and_2_out, and_3_out, and_4_out, and_5_out, and_6_out, and_7_out, and_8_out, and_9_out,
       and_10_out;

  and and_1 (and_1_out, P1, P2, G0);
  and and_2 (and_2_out, G1, P2, P3);
  and and_3 (and_3_out, G0, P1);
  and and_4 (and_4_out, G1, P2);
  and and_5 (and_5_out, P3, G2);
  and and_6 (and_6_out, P3, P2, P1, G0);
  and and_7 (and_7_out, P3, P2, P1, P0, Cin);
  or or_1 (C1, G0, and_8_out);
  and and_8 (and_8_out, P0, Cin);
  or or_2 (C2, G1, and_3_out, and_9_out);
  and and_9 (and_9_out, P0, P1, Cin);
  or or_3 (C3, G2, and_4_out, and_1_out, and_10_out);
  and and_10 (and_10_out, Cin, P2, P1, P0);
  or or_4 (C4, G3, and_5_out, and_2_out, and_6_out, and_7_out);

  assign C0 = Cin;
endmodule

module XOR4 (
  input  [3:0] A,
  input  [3:0] B,
  output [3:0] x
);

  xor xor_1 (x[0], B[0], A[0]);
  xor xor_2 (x[1], B[1], A[1]);
  xor xor_3 (x[2], B[2], A[2]);
  xor xor_4 (x[3], B[3], A[3]);
  // Probe on A
  // Probe on x
  // Probe on B
endmodule

module AND4 (
  input  [3:0] A,
  input  [3:0] B,
  output [3:0] nd
);

  // Probe on A
  // Probe on B
  and and_1 (nd[0], B[0], A[0]);
  and and_2 (nd[1], B[1], A[1]);
  and and_3 (nd[2], B[2], A[2]);
  and and_4 (nd[3], B[3], A[3]);
  // Probe on nd
endmodule

module OR4 (
  input  [3:0] A,
  input  [3:0] B,
  output [3:0] nd
);

  // Probe on A
  // Probe on B
  or or_1 (nd[0], B[0], A[0]);
  or or_2 (nd[1], B[1], A[1]);
  or or_3 (nd[2], B[2], A[2]);
  or or_4 (nd[3], B[3], A[3]);
  // Probe on nd
endmodule

module CLA16_Adder (
  input  [15:0] A,
  input  [15:0] B,
  input  Cin,
  output [15:0] S,
  output G,
  output P,
  output C
);

  wire [3:0] cla4_1_c0, cla4_adder_4_g, cla4_adder_4_p;

  // Probe on A
  // Probe on B
  CLA4_Adder cla4_adder_1 (
    .B(A[15:12]), .A(B[15:12]), .Cin(cla4_1_c0[3]), .P(cla4_adder_4_p[3]), .G(cla4_adder_4_g[3]), .S(S[15:12]));  // open: C
  CLA4_Adder cla4_adder_2 (
    .B(A[11:8]), .A(B[11:8]), .Cin(cla4_1_c0[2]), .P(cla4_adder_4_p[2]), .G(cla4_adder_4_g[2]), .S(S[11:8]));  // open: C
  CLA4_Adder cla4_adder_3 (
    .B(A[7:4]), .A(B[7:4]), .Cin(cla4_1_c0[1]), .P(cla4_adder_4_p[1]), .G(cla4_adder_4_g[1]), .S(S[7:4]));  // open: C
  gGen ggen_1 (.pi(cla4_adder_4_p), .gi(cla4_adder_4_g), .g(G));
  pgen pgen_1 (.pi(cla4_adder_4_p), .p(P));
  // Probe on S
  CLA4_Adder cla4_adder_4 (
    .B(A[3:0]), .A(B[3:0]), .Cin(cla4_1_c0[0]), .P(cla4_adder_4_p[0]), .G(cla4_adder_4_g[0]), .S(S[3:0]));  // open: C
  CLA4 cla4_1 (
    .G2(cla4_adder_4_g[2]), .G3(cla4_adder_4_g[3]), .G0(cla4_adder_4_g[0]), .G1(cla4_adder_4_g[1]),
    .P2(cla4_adder_4_p[2]), .P3(cla4_adder_4_p[3]), .Cin(Cin), .P0(cla4_adder_4_p[0]),
    .P1(cla4_adder_4_p[1]), .C1(cla4_1_c0[1]), .C2(cla4_1_c0[2]), .C3(cla4_1_c0[3]), .C4(C), .C0(cla4_1_c0[0]));
endmodule

module CLA29_Adder (
  input  [28:0] A,
  input  [28:0] B,
  input  Cin,
  output [28:0] S,
  output C
);

  wire cla4_1_c2;
  wire [1:0] cla4_1_c0, cla16_adder_2_g, cla16_adder_2_p;
  wire [15:14] cla16_adder_1_s;

  // Probe on A
  CLA16_Adder cla16_adder_1 (
    .A({{4{A[28]}}, A[27:16]}), .B({3'b000, B[28:16]}), .Cin(cla4_1_c0[1]), .G(cla16_adder_2_g[1]),
    .P(cla16_adder_2_p[1]), .S({cla16_adder_1_s, C, S[28:16]}));  // open: C
  CLA4 cla4_1 (
    .G2(1'b0), .G3(1'b0), .G0(cla16_adder_2_g[0]), .G1(cla16_adder_2_g[1]), .P2(1'b0), .P3(1'b0), .Cin(Cin),
    .P0(cla16_adder_2_p[0]), .P1(cla16_adder_2_p[1]), .C1(cla4_1_c0[1]), .C2(cla4_1_c2), .C0(cla4_1_c0[0]));  // open: C3, C4
  CLA16_Adder cla16_adder_2 (
    .A(A[15:0]), .B(B[15:0]), .Cin(cla4_1_c0[0]), .G(cla16_adder_2_g[0]), .P(cla16_adder_2_p[0]), .S(S[15:0]));  // open: C
  // Probe on S
endmodule

module XOR29 (
  input  [28:0] in_1,
  input  [28:0] in_2,
  output [28:0] out_3
);

  xor xor_1 (out_3[28], in_2[28], in_1[28]);
  XOR4 xor4_1 (.B(in_2[27:24]), .A(in_1[27:24]), .x(out_3[27:24]));
  XOR4 xor4_2 (.B(in_2[23:20]), .A(in_1[23:20]), .x(out_3[23:20]));
  XOR4 xor4_3 (.B(in_2[19:16]), .A(in_1[19:16]), .x(out_3[19:16]));
  XOR4 xor4_4 (.B(in_2[15:12]), .A(in_1[15:12]), .x(out_3[15:12]));
  XOR4 xor4_5 (.B(in_2[11:8]), .A(in_1[11:8]), .x(out_3[11:8]));
  XOR4 xor4_6 (.B(in_2[7:4]), .A(in_1[7:4]), .x(out_3[7:4]));
  XOR4 xor4_7 (.B(in_2[3:0]), .A(in_1[3:0]), .x(out_3[3:0]));

  // Other names for the same wires on the sheet: j = in_2[28]
endmodule

module AND29 (
  input  [28:0] in_1,
  input  [28:0] in_2,
  output [28:0] out_3
);

  and and_1 (out_3[28], in_2[28], in_1[28]);
  AND4 and4_1 (.A(in_1[27:24]), .B(in_2[27:24]), .nd(out_3[27:24]));
  AND4 and4_2 (.A(in_1[23:20]), .B(in_2[23:20]), .nd(out_3[23:20]));
  AND4 and4_3 (.A(in_1[19:16]), .B(in_2[19:16]), .nd(out_3[19:16]));
  AND4 and4_4 (.A(in_1[15:12]), .B(in_2[15:12]), .nd(out_3[15:12]));
  AND4 and4_5 (.A(in_1[11:8]), .B(in_2[11:8]), .nd(out_3[11:8]));
  AND4 and4_6 (.A(in_1[7:4]), .B(in_2[7:4]), .nd(out_3[7:4]));
  AND4 and4_7 (.A(in_1[3:0]), .B(in_2[3:0]), .nd(out_3[3:0]));

  // Other names for the same wires on the sheet: j = in_2[28]
endmodule

module OR29 (
  input  [28:0] in_1,
  input  [28:0] in_2,
  output [28:0] out_3
);

  or or_1 (out_3[28], in_2[28], in_1[28]);
  OR4 or4_1 (.A(in_1[27:24]), .B(in_2[27:24]), .nd(out_3[27:24]));
  OR4 or4_2 (.A(in_1[23:20]), .B(in_2[23:20]), .nd(out_3[23:20]));
  OR4 or4_3 (.A(in_1[19:16]), .B(in_2[19:16]), .nd(out_3[19:16]));
  OR4 or4_4 (.A(in_1[15:12]), .B(in_2[15:12]), .nd(out_3[15:12]));
  OR4 or4_5 (.A(in_1[11:8]), .B(in_2[11:8]), .nd(out_3[11:8]));
  OR4 or4_6 (.A(in_1[7:4]), .B(in_2[7:4]), .nd(out_3[7:4]));
  OR4 or4_7 (.A(in_1[3:0]), .B(in_2[3:0]), .nd(out_3[3:0]));

  // Other names for the same wires on the sheet: j = in_2[28]
endmodule

module Is_Zero (
  input  [28:0] inp,
  output isz
);

  nor nor_1 (isz, inp[0], inp[1], inp[2], inp[3], inp[4], inp[5], inp[6], inp[7], inp[8], inp[9], inp[10], inp[11], inp[12], inp[13], inp[14], inp[15], inp[16], inp[17], inp[18], inp[19], inp[20], inp[21], inp[22], inp[23], inp[24], inp[25], inp[26], inp[27], inp[28]);
endmodule

module cpy29 (
  input  in_1,
  output [28:0] out_2
);


  assign out_2 = {29{in_1}};
endmodule

module th28 (
  input  [28:0] in_1,
  output out_2
);


  assign out_2 = in_1[28];
endmodule

module Add_Sub (
  input  [28:0] B,
  input  [28:0] A,
  input  Cin,
  output [28:0] Sum,
  output C
);

  wire [28:0] cpy29_1_out_2, xor29_1_out_3;

  cpy29 cpy29_1 (.in_1(Cin), .out_2(cpy29_1_out_2));
  XOR29 xor29_1 (.in_2(B), .in_1(cpy29_1_out_2), .out_3(xor29_1_out_3));
  CLA29_Adder cla29_adder_1 (.B(xor29_1_out_3), .A(A), .Cin(Cin), .S(Sum), .C(C));
endmodule

module ALU (
  input  [3:0] Control,
  input  [28:0] A,
  input  [28:0] B,
  output [28:0] ALU_OUT
);

  wire [28:0] add_sub_1_sum, add_sub_2_sum, and29_1_out_3, divider_1_out, divider_1_rem, multiplier_1_cout,
       multiplier_1_out, not_1_out, or29_1_out_3, shifter_1_out, shifter_2_out, shifter_3_out, shifter_4_out,
       shifter_5_out, xor29_1_out_3;

  Add_Sub add_sub_1 (.A(B), .B(A), .Cin(1'b0), .Sum(add_sub_1_sum));  // open: C
  Add_Sub add_sub_2 (.A(B), .B(A), .Cin(1'b1), .Sum(add_sub_2_sum));  // open: C
  Multiplier #(.mode("twosComplement"), .width(29)) multiplier_1 (
    .a(A), .b(B), .out(multiplier_1_out), .cout(multiplier_1_cout));  // open: cin
  Divider #(.mode("twosComplement"), .width(29)) divider_1 (
    .a(A), .b(B), .out(divider_1_out), .rem(divider_1_rem));  // open: upper
  assign not_1_out = ~A;  // NOT_Gate not_1, 29 bits wide
  AND29 and29_1 (.in_2(B), .in_1(A), .out_3(and29_1_out_3));
  OR29 or29_1 (.in_2(B), .in_1(A), .out_3(or29_1_out_3));
  XOR29 xor29_1 (.in_2(B), .in_1(A), .out_3(xor29_1_out_3));
  Shifter #(.width(29)) shifter_1 (.in(A), .\dist (B[4:0]), .out(shifter_1_out));
  Shifter #(.shift("lr"), .width(29)) shifter_2 (.in(A), .\dist (B[4:0]), .out(shifter_2_out));
  Shifter #(.shift("rl"), .width(29)) shifter_3 (.in(A), .\dist (B[4:0]), .out(shifter_3_out));
  Shifter #(.shift("rr"), .width(29)) shifter_4 (.in(A), .\dist (B[4:0]), .out(shifter_4_out));
  Shifter #(.shift("ar"), .width(29)) shifter_5 (.in(A), .\dist (B[4:0]), .out(shifter_5_out));
  Multiplexer #(.select(4), .width(29)) multiplexer_1 (
    .in0(A), .in1(add_sub_1_sum), .in2(add_sub_2_sum), .in3(multiplier_1_out), .in4(multiplier_1_cout),
    .in5(divider_1_out), .in6(divider_1_rem), .in7(not_1_out), .in8(and29_1_out_3), .in9(or29_1_out_3),
    .in10(xor29_1_out_3), .in11(shifter_1_out), .in12(shifter_2_out), .in13(shifter_3_out),
    .in14(shifter_4_out), .in15(shifter_5_out), .out(ALU_OUT), .sel(Control));

  // Notes on the sheet:
  //   add
  //   sub
  //   mul
  //   mulh
endmodule

module reg29 (
  input  [28:0] D,
  input  clk,
  output [28:0] Q
);

  Register #(.width(29)) register_1 (.D(D), .en(1'b1), .clk(clk), .Q(Q), .clr(1'b0));
endmodule

module reg29f (
  input  [28:0] D,
  input  clk,
  output [28:0] Q
);

  Register #(.width(29)) register_1 (.D(D), .en(1'b1), .clk(clk), .Q(Q), .clr(1'b0));
endmodule

module enc2 (
  input  i0,
  input  i1,
  input  i3,
  input  i2,
  output [1:0] enc
);

  or or_1 (enc[0], i1, i3);
  or or_2 (enc[1], i3, i2);
endmodule

module reg4 (
  input  [3:0] d,
  input  en,
  input  c,
  output [3:0] q
);

  wire not_1_out;

  Register #(.width(4)) register_1 (.D(d), .en(not_1_out), .clk(c), .Q(q), .clr(en));
  not not_1 (not_1_out, en);
  LED overflow (.in(q[3]));
  LED carry (.in(q[2]));
  LED neg (.in(q[1]));
  LED zero (.in(q[0]));
endmodule

module pgen (
  input  [3:0] pi,
  output p
);

  and and_1 (p, pi[0], pi[1], pi[2], pi[3]);
endmodule

module gGen (
  input  [3:0] pi,
  input  [3:0] gi,
  output g
);

  wire and_1_out, and_2_out, and_3_out;

  and and_1 (and_1_out, pi[1], pi[2], pi[3], gi[0]);
  and and_2 (and_2_out, pi[3], pi[2], gi[1]);
  and and_3 (and_3_out, pi[3], gi[2]);
  or or_1 (g, and_1_out, and_2_out, and_3_out, gi[3]);
endmodule

module multpx (
  input  [28:0] i0,
  input  S,
  input  [28:0] i1,
  output [28:0] Y
);

  wire [28:0] and_1_out, and_2_out, cpy29_1_out_2;

  cpy29 cpy29_1 (.in_1(S), .out_2(cpy29_1_out_2));
  assign and_1_out = i0 & ~cpy29_1_out_2;  // AND_Gate and_1, 29 bits wide
  assign and_2_out = cpy29_1_out_2 & i1;  // AND_Gate and_2, 29 bits wide
  assign Y = and_1_out | and_2_out;  // OR_Gate or_1, 29 bits wide
endmodule

module multpxb (
  input  [28:0] i0,
  input  S,
  input  [28:0] i1,
  output [28:0] Y
);

  wire [28:0] and_1_out, and_2_out, cpy29_1_out_2;

  cpy29 cpy29_1 (.in_1(S), .out_2(cpy29_1_out_2));
  assign and_1_out = i0 & ~cpy29_1_out_2;  // AND_Gate and_1, 29 bits wide
  assign and_2_out = cpy29_1_out_2 & i1;  // AND_Gate and_2, 29 bits wide
  assign Y = and_1_out | and_2_out;  // OR_Gate or_1, 29 bits wide
endmodule

module sw (
  input  S,
  output Y
);

  wire and_1_out, and_2_out;

  and and_1 (and_1_out, 1'b0, ~S);  // AND_Gate
  and and_2 (and_2_out, S, 1'b1);
  or or_1 (Y, and_1_out, and_2_out);
endmodule

module one (
  output out_1
);


  assign out_1 = 1'b1;
endmodule

module Booths (
);

  ALU alu_1 ();  // open: B, Control, A, ALU_OUT
endmodule

module ShiftD29 (
  input  [7:0] in_1,
  input  [1:0] in_2,
  input  in_3,
  input  [1:0] in_4,
  input  in_5,
  input  [7:0] in_6,
  input  [7:0] in_7
);

  wire clock_1_out, decoder_1_out1, decoder_1_out2, decoder_1_out3, or_1_out, or_2_out, or_3_out;
  wire [7:0] d1, d2, d3, multiplexer_1_out, multiplexer_2_out, multiplexer_3_out, multiplexer_4_out, q1, q2,
       q3;

  Multiplexer #(.select(2), .width(8)) multiplexer_1 (
    .in1(q1), .in2(q2), .in3(q3), .out(multiplexer_1_out), .sel(in_2));  // open: in0
  Demultiplexer #(.select(2), .width(8)) demultiplexer_1 (
    .out1(d1), .out2(d2), .out3(d3), .in(multiplexer_1_out), .sel(in_4));  // open: out0
  Decoder #(.select(2)) decoder_1 (
    .out1(decoder_1_out1), .out2(decoder_1_out2), .out3(decoder_1_out3), .sel(in_4), .en(1'b1));  // open: out0
  Multiplexer #(.width(8)) multiplexer_2 (.in0(d3), .in1(in_7), .out(multiplexer_2_out), .sel(in_5));
  Clock clock_1 (.out(clock_1_out));
  Multiplexer #(.width(8)) multiplexer_3 (.in0(d1), .in1(in_1), .out(multiplexer_3_out), .sel(in_5));
  Multiplexer #(.width(8)) multiplexer_4 (.in0(d2), .in1(in_6), .out(multiplexer_4_out), .sel(in_5));
  or or_1 (or_1_out, in_5, decoder_1_out2);
  or or_2 (or_2_out, in_5, decoder_1_out3);
  Register register_1 (.D(multiplexer_3_out), .en(or_3_out), .clk(clock_1_out), .Q(q1), .clr(in_3));
  or or_3 (or_3_out, in_5, decoder_1_out1);
  Register register_2 (.D(multiplexer_4_out), .en(or_1_out), .clk(clock_1_out));  // open: Q, clr
  Register register_3 (.D(multiplexer_2_out), .en(or_2_out), .clk(clock_1_out), .Q(q3));  // open: clr

  // Other names for the same wires on the sheet: go = in_5
endmodule
