// Logisim project CPU.circ as structural Verilog
module main (
  input  [28:0] in_1,
  input  in_2,
  input  in_3,
  input  in_4,
  input  in_5,
  input  in_6,
  input  in_7,
  input  in_8,
  input  in_9,
  input  in_10,
  input  in_11,
  input  in_12,
  input  in_13,
  input  in_14,
  input  in_15,
  input  in_16,
  input  in_17,
  input  in_18,
  input  in_19,
  input  in_20,
  input  in_21,
  input  in_22,
  input  in_23,
  input  in_24,
  input  in_25,
  input  in_26,
  input  in_27,
  input  in_28,
  input  in_29,
  input  in_30,
  input  in_31,
  input  [28:0] in_32,
  input  in_33,
  input  reset
);

  wire and_3_out, bu_1_update, clk, comparator_1_lt, draw, ex_st_ld, exmem_1_je, hlt, \int , jmp, kin,
       m_st_ld, mcl, not_1_out, outON, rgb_video_1_p2, rgb_video_1_p3, rgb_video_1_p4, selio, undriven,
       wb_write;
  wire [1:0] exsc;
  wire [3:0] exaluc, joystick_1_x, joystick_1_y, parser_1_alu_control, rgb_video_1_p5, rgb_video_1_p6;
  wire [4:0] ifid_1_a, ifid_1_b, parser_1_a, parser_1_b, parser_1_c, wb_loc;
  wire [5:0] exmem_1_meo, exmem_1_write_back, idex_1_execution, idex_1_memory, idex_1_write_back,
       ifid_1_execution, ifid_1_memory, ifid_1_write_back, parser_1_opcode;
  wire [6:0] keyboard_1_data;
  wire [11:0] parser_1_immediate;
  wire [12:0] parser_1_jump_relative;
  wire [15:0] bu_1_pc_out, dor_matrox_control_1_out_2, dor_matrox_control_1_out_3,
       dor_matrox_control_1_out_4, dor_matrox_control_1_out_5, dor_matrox_control_1_out_6,
       dor_matrox_control_1_out_7, dor_matrox_control_1_out_8, dor_matrox_control_1_out_9,
       dor_matrox_control_1_out_10, dor_matrox_control_1_out_11, dor_matrox_control_1_out_12,
       dor_matrox_control_1_out_13, dor_matrox_control_1_out_14, dor_matrox_control_1_out_15,
       dor_matrox_control_1_out_16, dor_matrox_control_1_out_17, exmem_1_pc, expc, fd, idex_1_ld, idex_1_st,
       ifid_1_pc_out, iomar, multiplexer_8_out, parser_1_load_addr, parser_1_store_addr, pc_1_pc_out,
       where_to;
  wire [16:0] parser_1_imm_up;
  wire [23:0] rgb_video_1_p7;
  wire [28:0] alu_1_alu_out, custom, datain, displayIn, dmIn, exa, exb, exir, exmem_1_eir, idex_1_b,
       idex_1_im, ifid_1_ir_out, IOout, keyIn, keyOut, lui, mb, memalu, multiplexer_2_out, multiplexer_3_out,
       multiplexer_6_out, ram_1_dout, registerfile_1_a, registerfile_1_b, rom_1_data, Seg7In, stickOut,
       ttyIn, wb_data;

  ttycontroller ttycontroller_1 (.in_2(ttyIn), .clk(mcl));
  Keyboard #(.buflen(128)) keyboard_1 (.clk(mcl), .re(kin), .clr(undriven), .data(keyboard_1_data));  // open: avail
  Seg7Controller seg7controller_1 (.clk(mcl), .data(Seg7In));  // open: rst
  PC pc_1 (
    .increment(not_1_out), .clk(clk), .data_in(where_to), .reset(reset), .load(jmp), .pc_out(pc_1_pc_out));  // open: overflow
  not not_1 (not_1_out, jmp);
  Clock clock_1 (.out(mcl));
  and and_1 (clk, mcl, ~\int , ~hlt);  // AND_Gate
  ROM #(.addrWidth(10), .dataWidth(29)) rom_1 (.addr(pc_1_pc_out[9:0]), .data(rom_1_data));
  RAM #(.addrWidth(16), .asyncread("true"), .dataWidth(29)) ram_1 (
    .addr(pc_1_pc_out), .we(1'b0), .oe(1'b1), .clk(clk), .dout(ram_1_dout));  // open: din
  KeyboardController keyboardcontroller_1 (.in_1(keyboard_1_data), .out_2(keyOut));
  Multiplexer #(.width(29)) multiplexer_1 (
    .in0({in_3, in_4, in_5, in_6, in_7, in_8, in_9, in_10, in_11, in_12, in_13, in_14, in_15, in_16, in_17, in_18, in_19, in_20, in_21, in_22, in_23, in_24, in_25, in_26, in_27, in_28, in_29, in_30, in_31}),
    .in1(in_32), .out(custom));  // open: sel
  // RGB_Video #(.cursor("No Cursor"), .height(16), .scale(8), .width(16)) rgb_video_1: pin names not known; wires that end beside it: in_33, rgb_video_1_p2, rgb_video_1_p3, rgb_video_1_p4, rgb_video_1_p5, rgb_video_1_p6, rgb_video_1_p7
  VideoController videocontroller_1 (
    .clki(mcl), .din(displayIn), .draw(draw), .clr(reset), .mb(mb), .clko(rgb_video_1_p3), .\int (\int ),
    .mar(iomar), .RD(rgb_video_1_p2), .D(rgb_video_1_p4), .x(rgb_video_1_p5), .y(rgb_video_1_p6),
    .color(rgb_video_1_p7));
  Joystick joystick_1 (.x(joystick_1_x), .y(joystick_1_y));
  joysplit joysplit_1 (.in_2(joystick_1_y), .in_1(joystick_1_x), .out_3(stickOut));
  Comparator #(.width(16)) comparator_1 (.a(16'h400), .b(pc_1_pc_out), .lt(comparator_1_lt));  // open: gt, eq
  Multiplexer #(.width(29)) multiplexer_2 (
    .in0(rom_1_data), .in1(ram_1_dout), .out(multiplexer_2_out), .sel(comparator_1_lt));
  Multiplexer #(.width(29)) multiplexer_3 (.in0(multiplexer_2_out), .in1(custom), .out(multiplexer_3_out), .sel(in_2));
  // Probe on parser_1_jump_relative
  // Probe on parser_1_imm_up
  // Probe on parser_1_immediate
  // Probe on parser_1_load_addr
  // Probe on parser_1_store_addr
  DotMatrix #(.inputtype("row"), .matrixcols(16), .matrixrows(16), .persist(16)) dotmatrix_1 (
    .row0(dor_matrox_control_1_out_2), .row1(dor_matrox_control_1_out_3), .row2(dor_matrox_control_1_out_4),
    .row3(dor_matrox_control_1_out_5), .row4(dor_matrox_control_1_out_6), .row5(dor_matrox_control_1_out_7),
    .row6(dor_matrox_control_1_out_8), .row7(dor_matrox_control_1_out_9), .row8(dor_matrox_control_1_out_10),
    .row9(dor_matrox_control_1_out_11), .row10(dor_matrox_control_1_out_12),
    .row11(dor_matrox_control_1_out_13), .row12(dor_matrox_control_1_out_14),
    .row13(dor_matrox_control_1_out_15), .row14(dor_matrox_control_1_out_16),
    .row15(dor_matrox_control_1_out_17));
  dor_matrox_control dor_matrox_control_1 (
    .in_1(dmIn), .out_3(dor_matrox_control_1_out_3), .out_5(dor_matrox_control_1_out_5),
    .out_7(dor_matrox_control_1_out_7), .out_9(dor_matrox_control_1_out_9),
    .out_11(dor_matrox_control_1_out_11), .out_13(dor_matrox_control_1_out_13),
    .out_15(dor_matrox_control_1_out_15), .out_17(dor_matrox_control_1_out_17),
    .out_4(dor_matrox_control_1_out_4), .out_6(dor_matrox_control_1_out_6),
    .out_8(dor_matrox_control_1_out_8), .out_10(dor_matrox_control_1_out_10),
    .out_12(dor_matrox_control_1_out_12), .out_14(dor_matrox_control_1_out_14),
    .out_16(dor_matrox_control_1_out_16), .out_2(dor_matrox_control_1_out_2));
  // Probe on multiplexer_3_out
  Parser parser_1 (
    .IR(multiplexer_3_out), .Imm_UP(parser_1_imm_up), .Load_addr(parser_1_load_addr),
    .Store_addr(parser_1_store_addr), .jump_relative(parser_1_jump_relative), .Immediate(parser_1_immediate),
    .C(parser_1_c), .A(parser_1_a), .B(parser_1_b), .opcode(parser_1_opcode),
    .ALU_CONTROL(parser_1_alu_control));
  // Probe on parser_1_opcode
  // Probe on parser_1_a
  // Probe on parser_1_b
  // Probe on parser_1_c
  // Probe on parser_1_alu_control
  // Probe on parser_1_opcode
  // Probe on parser_1_a
  // Probe on parser_1_b
  // Probe on parser_1_c
  IFID ifid_1 (
    .PC_IN(pc_1_pc_out), .IR_IN(multiplexer_3_out), .clk(clk), .reset(reset), .PC_OUT(ifid_1_pc_out),
    .IR_OUT(ifid_1_ir_out), .execution(ifid_1_execution), .memory(ifid_1_memory),
    .write_back(ifid_1_write_back), .A(ifid_1_a), .B(ifid_1_b));
  RegisterFile registerfile_1 (
    .adr_a(ifid_1_a), .adr_b(ifid_1_b), .write_to(wb_loc), .data(wb_data), .clock(clk), .write(wb_write),
    .reset(reset), .a(registerfile_1_a), .b(registerfile_1_b));
  IDEX idex_1 (
    .PC_IN(ifid_1_pc_out), .B_addr(registerfile_1_b), .A_addr(registerfile_1_a), .IR_IN(ifid_1_ir_out),
    .in_5(clk), .in_6(reset), .mei(ifid_1_memory), .wbi(ifid_1_write_back), .exi(ifid_1_execution),
    .B(idex_1_b), .A(exa), .IR_OUT(exir), .IM(idex_1_im), .PC_OUT(expc), .ALU_CONTROL(exaluc), .IMU(lui),
    .ld(idex_1_ld), .st(idex_1_st), .memory(idex_1_memory), .write_back(idex_1_write_back),
    .execution({idex_1_execution[5], hlt, ex_st_ld, exsc, idex_1_execution[0]}));
  Multiplexer #(.width(29)) multiplexer_4 (.in0(idex_1_b), .in1(idex_1_im), .out(exb), .sel(idex_1_execution[0]));
  Multiplexer #(.width(16)) multiplexer_5 (.in0(idex_1_st), .in1(idex_1_ld), .out(fd), .sel(ex_st_ld));
  BU bu_1 (.A(exa), .B(exb), .PC(expc), .IR(exir), .PC_OUT(bu_1_pc_out), .update(bu_1_update));
  ALU alu_1 (.B(exb), .Control(exaluc), .A(exa), .ALU_OUT(alu_1_alu_out));
  Multiplexer #(.select(2), .width(29)) multiplexer_6 (
    .in0(exa), .in1(alu_1_alu_out), .in2(lui), .in3({{13{1'b0}}, fd}), .out(multiplexer_6_out));  // open: sel
  EXMEM exmem_1 (
    .B(exb), .ir(exir), .j(bu_1_update), .mei(idex_1_memory), .alui(multiplexer_6_out), .jmp(bu_1_pc_out),
    .wbi(idex_1_write_back), .clk(clk), .reset(reset), .pci(expc),
    .meo({exmem_1_meo[5:4], outON, selio, m_st_ld, exmem_1_meo[0]}), .Bout(datain), .eir(exmem_1_eir),
    .je(exmem_1_je), .write_back(exmem_1_write_back), .alu(memalu), .jmp2(where_to), .pc(exmem_1_pc));
  and and_2 (jmp, exmem_1_meo[0], exmem_1_je);
  Decoder #(.select(3)) decoder_1 (
    .out2(draw), .out3(kin), .sel(memalu[2:0]), .en(selio));  // open: out0, out1, out4, out5, out6, out7
  Multiplexer #(.disabled("Z"), .enable("true"), .select(3), .width(29)) multiplexer_7 (
    .in3(keyOut), .in4(in_1), .in5(stickOut), .out(IOout));  // open: in0, in1, in2, in6, in7, sel, en
  Demultiplexer #(.enable("true"), .select(3), .tristate("true"), .width(29)) demultiplexer_1 (
    .out0(ttyIn), .out1(Seg7In), .out2(displayIn), .out3(keyIn), .out6(dmIn), .in(datain), .sel(memalu[2:0]),
    .en(selio));  // open: out4, out5, out7
  RAM #(.addrWidth(16), .asyncread("true"), .dataWidth(29), .\type ("nonvolatile")) ram_2 (
    .addr(multiplexer_8_out), .we(and_3_out), .oe(1'b1), .clk(mcl), .din(datain), .dout(mb));
  Multiplexer #(.width(16)) multiplexer_8 (.in0(memalu[15:0]), .in1(iomar), .out(multiplexer_8_out), .sel(selio));
  and and_3 (and_3_out, m_st_ld, ~selio);  // AND_Gate
  MEMWB memwb_1 (
    .wbi(exmem_1_write_back), .IR_IN(exmem_1_eir), .pci(exmem_1_pc), .iRAM(mb), .iALU(memalu), .ioO(IOout),
    .clk(clk), .reset(reset), .write(wb_write), .to_reg(wb_loc), .to_be_written(wb_data));  // open: IR_OUT

  // Other names for the same wires on the sheet: custom_enable = in_2; IOIN[28:0] = datain; imOut[28:0] = in_1;
  //   rdio[2:0] = memalu[2:0]; rst = reset

  // Notes on the sheet:
  //   contents of rom_1 (hex, n*v repeats v):
  //   140291 5*0 40051 4*0 a082a 5*0 280291 5*0 60051 4*0 a082a 5*0 40051 4*0 aa8 7*0 21092 a102a 5*0
  //   60051 4*0 aa8 7*0 a02c1 5*0 12a8 21091 5*0 b5281 5*0 80051 4*0 a082a 5*0 291 5*0 a02c1 5*0 7020 5*0
  //   2c1 5*0 7020
endmodule

module PC (
  input  reset,
  input  load,
  input  increment,
  input  clk,
  input  [15:0] data_in,
  output overflow,
  output [15:0] pc_out
);

  Counter #(.max('hffff), .width(16)) counter_1 (
    .clr(reset), .load(load), .up(1'b1), .count(increment), .clk(clk), .D(data_in), .carry(overflow),
    .Q(pc_out));
endmodule

module IR (
  input  [28:0] ir_in,
  input  write,
  input  clk,
  input  reset,
  output [28:0] ir_out
);

  Register #(.width(29)) register_1 (.D(ir_in), .en(write), .clk(clk), .Q(ir_out), .clr(reset));
endmodule

module CUPC (
  input  reset,
  input  load,
  input  overflow,
  input  increment,
  input  clk,
  input  [2:0] data_in,
  input  [2:0] pc_out
);

  Counter #(.max('h7), .width(3)) counter_1 (
    .clr(reset), .load(load), .up(1'b1), .count(increment), .clk(clk), .D(data_in), .carry(overflow),
    .Q(pc_out));
endmodule

module CU (
  input  [28:0] IR,
  output [5:0] Execution,
  output [5:0] Memory,
  output [5:0] WriteBack
);

  wire [5:0] parser_1_opcode;

  Parser parser_1 (
    .IR(IR), .opcode(parser_1_opcode));  // open: Imm_UP, Load_addr, Store_addr, jump_relative, Immediate, C, A, B, ALU_CONTROL
  ROM #(.addrWidth(6), .dataWidth(6)) rom_1 (.addr(parser_1_opcode), .data(Execution));
  ROM #(.addrWidth(6), .dataWidth(6)) rom_2 (.addr(parser_1_opcode), .data(Memory));
  ROM #(.addrWidth(6), .dataWidth(6)) rom_3 (.addr(parser_1_opcode), .data(WriteBack));

  // Notes on the sheet:
  //   contents of rom_1 (hex, n*v repeats v):
  //   15*2 3 0 6*3 4 8*3 9*0 6 8 e 0 6 8 e 15*0 10
  //   contents of rom_2 (hex, n*v repeats v):
  //   32*0 8*1 0 0 2 2 4 4 c c
  //   contents of rom_3 (hex, n*v repeats v):
  //   16*1 0 15*1 7*0 7 3 3 0 0 5 5
endmodule

module Parser (
  input  [28:0] IR,
  output [5:0] opcode,
  output [3:0] ALU_CONTROL,
  output [4:0] C,
  output [4:0] A,
  output [4:0] B,
  output [11:0] Immediate,
  output [16:0] Imm_UP,
  output [15:0] Load_addr,
  output [15:0] Store_addr,
  output [12:0] jump_relative
);


  assign A = IR[15:11];
  assign ALU_CONTROL = IR[3:0];
  assign B = IR[20:16];
  assign C = IR[10:6];
  assign Imm_UP = IR[28:12];
  assign Immediate = IR[28:17];
  assign jump_relative = {IR[28:21], IR[10:6]};
  assign Load_addr = IR[28:13];
  assign opcode = IR[5:0];
  assign Store_addr = {IR[28:23], IR[15:6]};

  // Other names for the same wires on the sheet: store1st[4:0] = IR[10:6]; store2nd[4:0] = IR[15:11]

  // Notes on the sheet:
  //   opcode
  //   alu
  //   rd
  //   rs1
  //   rs2
endmodule

module IFID (
  input  [28:0] IR_IN,
  input  [15:0] PC_IN,
  input  clk,
  input  reset,
  output [5:0] execution,
  output [5:0] memory,
  output [5:0] write_back,
  output [4:0] A,
  output [4:0] B,
  output [28:0] IR_OUT,
  output [15:0] PC_OUT
);

  wire [5:0] parser_1_opcode;

  Register #(.width(29)) IR (.D(IR_IN), .en(1'b1), .clk(clk), .Q(IR_OUT), .clr(reset));
  Register #(.width(16)) PC (.D(PC_IN), .en(1'b1), .clk(clk), .Q(PC_OUT), .clr(reset));
  CU cu_1 (.IR(IR_OUT), .Memory(memory), .WriteBack(write_back), .Execution(execution));
  Parser parser_1 (
    .IR(IR_OUT), .A(A), .B(B), .opcode(parser_1_opcode));  // open: Imm_UP, Load_addr, Store_addr, jump_relative, Immediate, C, ALU_CONTROL
  // Probe on parser_1_opcode
endmodule

module BU (
  input  [28:0] IR,
  input  [15:0] PC,
  input  [28:0] A,
  input  [28:0] B,
  output [15:0] PC_OUT,
  output update
);

  wire comparator_2_eq, comparator_3_eq, comparator_4_eq, comparator_5_eq;
  wire [1:1] comparator_1_eq;
  wire [2:0] comparator_1_gt;
  wire [5:0] op;
  wire [12:0] jr;
  wire [15:0] adder_1_out, bit_extender_1_out, jaddr;

  Parser parser_1 (
    .IR(IR), .Load_addr(jaddr), .jump_relative(jr), .opcode(op));  // open: Imm_UP, Store_addr, Immediate, C, A, B, ALU_CONTROL
  Comparator #(.width(29)) comparator_1 (
    .a(A), .b(B), .gt(comparator_1_gt[0]), .eq(comparator_1_eq[1]), .lt(comparator_1_gt[2]));
  Adder #(.width(16)) adder_1 (.a(PC), .b(bit_extender_1_out), .out(adder_1_out));  // open: cin, cout
  assign bit_extender_1_out = {{3{jr[12]}}, jr};  // Bit_Extender bit_extender_1
  Comparator #(.width(3)) comparator_2 (.a(3'b111), .b(op[2:0]), .eq(comparator_2_eq));  // open: gt, lt
  Comparator #(.width(3)) comparator_3 (
    .a({1'b1, comparator_1_eq[1], 1'b1}), .b(op[2:0]), .eq(comparator_3_eq));  // open: gt, lt
  Comparator #(.width(3)) comparator_4 (
    .a(op[2:0]), .b({comparator_1_gt[2], comparator_1_eq[1], comparator_1_gt[0]}), .eq(comparator_4_eq));  // open: gt, lt
  Multiplexer #(.width(16)) multiplexer_1 (.in0(adder_1_out), .in1(jaddr), .out(PC_OUT), .sel(comparator_2_eq));
  Comparator #(.width(3)) comparator_5 (.a(3'b000), .b(op[2:0]), .eq(comparator_5_eq));  // open: gt, lt
  or or_1 (update, comparator_2_eq, comparator_3_eq, comparator_4_eq, comparator_5_eq);

  // Notes on the sheet:
  //   jz is done by comparing with r0
  //   unc - long
  //   ne
  //   un conditional
endmodule

module IDEX (
  input  [28:0] A_addr,
  input  [5:0] exi,
  input  [28:0] B_addr,
  input  [5:0] mei,
  input  in_5,
  input  in_6,
  input  [5:0] wbi,
  input  [28:0] IR_IN,
  input  [15:0] PC_IN,
  output [28:0] A,
  output [5:0] execution,
  output [28:0] B,
  output [5:0] memory,
  output [5:0] write_back,
  output [3:0] ALU_CONTROL,
  output [15:0] ld,
  output [15:0] st,
  output [28:0] IM,
  output [28:0] IMU,
  output [28:0] IR_OUT,
  output [15:0] PC_OUT
);

  wire [11:0] parser_1_immediate;

  Register #(.width(29)) register_1 (.D(A_addr), .en(1'b1), .clk(in_5), .Q(A), .clr(in_6));
  Register #(.width(29)) register_2 (.D(B_addr), .en(1'b1), .clk(in_5), .Q(B), .clr(in_6));
  Parser parser_1 (
    .IR(IR_OUT), .Imm_UP(IMU[28:12]), .Load_addr(st), .Store_addr(ld), .Immediate(parser_1_immediate),
    .ALU_CONTROL(ALU_CONTROL));  // open: jump_relative, C, A, B, opcode
  Register #(.width(29)) IR (.D(IR_IN), .en(1'b1), .clk(in_5), .Q(IR_OUT), .clr(in_6));
  Register #(.width(16)) PC (.D(PC_IN), .en(1'b1), .clk(in_5), .Q(PC_OUT), .clr(in_6));
  assign IM = {{17{parser_1_immediate[11]}}, parser_1_immediate};  // Bit_Extender bit_extender_1
  Register #(.width(6)) register_3 (.D(exi), .en(1'b1), .clk(in_5), .Q(execution), .clr(in_6));
  Register #(.width(6)) register_4 (.D(mei), .en(1'b1), .clk(in_5), .Q(memory), .clr(in_6));
  Register #(.width(6)) register_5 (.D(wbi), .en(1'b1), .clk(in_5), .Q(write_back), .clr(in_6));

  assign IMU[11:0] = {12{1'b0}};

  // Other names for the same wires on the sheet: clk = in_5; rst = in_6
endmodule

module EXMEM (
  input  [5:0] mei,
  input  [5:0] wbi,
  input  [28:0] alui,
  input  clk,
  input  reset,
  input  [15:0] jmp,
  input  [15:0] pci,
  input  [28:0] B,
  input  [28:0] ir,
  input  j,
  output [5:0] meo,
  output [5:0] write_back,
  output [28:0] alu,
  output [15:0] jmp2,
  output [15:0] pc,
  output [28:0] Bout,
  output [28:0] eir,
  output je
);

  Register #(.width(6)) register_1 (.D(mei), .en(1'b1), .clk(clk), .Q(meo), .clr(reset));
  Register #(.width(29)) register_2 (.D(B), .en(1'b1), .clk(clk), .Q(Bout), .clr(reset));
  Register #(.width(29)) register_3 (.D(ir), .en(1'b1), .clk(clk), .Q(eir), .clr(reset));
  Register #(.width(1)) register_4 (.D(j), .en(1'b1), .clk(clk), .Q(je), .clr(reset));
  Register #(.width(6)) register_5 (.D(wbi), .en(1'b1), .clk(clk), .Q(write_back), .clr(reset));
  Register #(.width(29)) register_6 (.D(alui), .en(1'b1), .clk(clk), .Q(alu), .clr(reset));
  Register #(.width(16)) register_7 (.D(jmp), .en(1'b1), .clk(clk), .Q(jmp2), .clr(reset));
  Register #(.width(16)) register_8 (.D(pci), .en(1'b1), .clk(clk), .Q(pc), .clr(reset));

  // Other names for the same wires on the sheet: rst = reset
endmodule

module MEMWB (
  input  [5:0] wbi,
  input  [28:0] iALU,
  input  [28:0] iRAM,
  input  [28:0] IR_IN,
  input  clk,
  input  reset,
  input  [28:0] ioO,
  input  [15:0] pci,
  output write,
  output [28:0] to_be_written,
  output [28:0] IR_OUT,
  output [4:0] to_reg
);

  wire [1:0] frmWhere;
  wire [5:3] register_1_q;
  wire [15:0] register_5_q;
  wire [28:0] bit_extender_1_out, register_3_q, register_4_q;

  Register #(.width(6)) register_1 (.D(wbi), .en(1'b1), .clk(clk), .Q({register_1_q, frmWhere, write}), .clr(reset));
  Register #(.width(29)) register_2 (.D(IR_IN), .en(1'b1), .clk(clk), .Q(IR_OUT), .clr(reset));
  Parser parser_1 (
    .IR(IR_OUT), .C(to_reg));  // open: Imm_UP, Load_addr, Store_addr, jump_relative, Immediate, A, B, opcode, ALU_CONTROL
  Register #(.width(29)) register_3 (.D(iALU), .en(1'b1), .clk(clk), .Q(register_3_q), .clr(reset));
  Register #(.width(29)) register_4 (.D(ioO), .en(1'b1), .clk(clk), .Q(register_4_q), .clr(reset));
  Register #(.width(16)) register_5 (.D(pci), .en(1'b1), .clk(clk), .Q(register_5_q), .clr(reset));
  assign bit_extender_1_out = {{13{register_5_q[15]}}, register_5_q};  // Bit_Extender bit_extender_1
  Multiplexer #(.select(2), .width(29)) multiplexer_1 (
    .in0(register_3_q), .in1(iRAM), .in2(register_4_q), .in3(bit_extender_1_out), .out(to_be_written),
    .sel(frmWhere));

  // Other names for the same wires on the sheet: rst = reset
endmodule

module DataMemory (
  input  [15:0] address,
  input  write,
  input  clk,
  input  [28:0] dataIn,
  output [28:0] data
);

  RAM #(.addrWidth(16), .dataWidth(29)) ram_1 (
    .addr(address), .we(write), .oe(1'b1), .clk(clk), .din(dataIn), .dout(data));
endmodule

module VideoController (
  input  clki,
  input  clr,
  input  draw,
  input  [28:0] mb,
  input  [28:0] din,
  output clko,
  output [3:0] x,
  output [23:0] color,
  output \int ,
  output RD,
  output D,
  output [3:0] y,
  output [15:0] mar
);

  wire ac, and_1_out, and_2_out, bc;
  wire [3:0] a, b;
  wire [15:0] adder_1_out, multiplier_1_out;

  and and_1 (and_1_out, draw, ~and_2_out);  // AND_Gate
  and and_2 (and_2_out, ac, bc);
  Multiplier #(.width(16)) multiplier_1 (.a({{12{1'b0}}, b}), .b(16'h10), .out(multiplier_1_out));  // open: cin, cout
  T_Flip_Flop t_ff_1 (.T(1'b1), .clk(and_1_out), .Q(\int ));  // open: Qn, reset, preset
  Adder #(.width(16)) adder_1 (.a(multiplier_1_out), .b({{12{1'b0}}, a}), .out(adder_1_out));  // open: cin, cout
  D_Flip_Flop d_ff_1 (.D(draw), .clk(clki), .Q(D));  // open: Qn, preset, reset
  Adder #(.width(16)) adder_2 (.a(din[15:0]), .b(adder_1_out), .out(mar));  // open: cin, cout
  or or_1 (RD, clr, clr);
  Counter #(.max('hf), .ongoal("continue"), .width(4)) counter_1 (
    .count(draw), .Q(a), .carry(ac), .up(1'b1), .clk(clki), .clr(clr));  // open: load, D
  Register #(.width(4)) register_1 (.D(a), .en(1'b1), .clk(clki), .Q(x), .clr(clr));
  Register #(.width(4)) register_2 (.D(b), .en(1'b1), .clk(clki), .Q(y), .clr(clr));
  Counter #(.max('hf), .ongoal("continue"), .trigger("falling"), .width(4)) counter_2 (
    .count(draw), .Q(b), .carry(bc), .up(1'b1), .clk(ac), .clr(clr));  // open: load, D

  assign clko = clki;
  assign color = mb[23:0];

  // Other names for the same wires on the sheet: clk = clki; d_t = draw; inaddr[15:0] = din[15:0]; rD_t = clr
endmodule

module Seg7Controller (
  input  [28:0] data,
  input  clk,
  input  rst
);

  wire [0:0] register_1_q_6;
  wire [3:0] register_1_q_2, register_1_q_3, register_1_q_4, register_1_q_5;
  wire [11:0] register_1_q;

  Register #(.width(29)) register_1 (
    .D(data), .en(1'b1), .clk(clk),
    .Q({register_1_q_6[0], register_1_q_5, register_1_q_4, register_1_q_3, register_1_q_2, register_1_q}),
    .clr(rst));
  Hex_Digit_Display hex_digit_display_1 (.value({3'b000, register_1_q_6[0]}));  // open: dp
  Hex_Digit_Display hex_digit_display_2 (.value(register_1_q_5));  // open: dp
  Hex_Digit_Display hex_digit_display_3 (.value(register_1_q_4));  // open: dp
  Hex_Digit_Display hex_digit_display_4 (.value(register_1_q_3));  // open: dp
  Hex_Digit_Display hex_digit_display_5 (.value(register_1_q_2));  // open: dp
  Hex_Digit_Display hex_digit_display_6 (.value(register_1_q[11:8]));  // open: dp
  Hex_Digit_Display hex_digit_display_7 (.value(register_1_q[7:4]));  // open: dp
  Hex_Digit_Display hex_digit_display_8 (.value(register_1_q[3:0]));  // open: dp
endmodule

module ttycontroller (
  input  clk,
  input  [28:0] in_2
);

  wire not_1_out;

  TTY #(.rows(10)) tty_1 (.data(in_2[6:0]), .clk(clk), .we(not_1_out), .clr(in_2[8]));
  not not_1 (not_1_out, in_2[7]);
endmodule

module KeyboardController (
  input  [6:0] in_1,
  output [28:0] out_2
);


  assign out_2 = {{22{1'b0}}, in_1};
endmodule

module joysplit (
  input  [3:0] in_1,
  input  [3:0] in_2,
  output [28:0] out_3
);


  assign out_3 = {{21{1'b0}}, in_2, in_1};
endmodule

module dor_matrox_control (
  input  [28:0] in_1,
  output [15:0] out_2,
  output [15:0] out_3,
  output [15:0] out_4,
  output [15:0] out_5,
  output [15:0] out_6,
  output [15:0] out_7,
  output [15:0] out_8,
  output [15:0] out_9,
  output [15:0] out_10,
  output [15:0] out_11,
  output [15:0] out_12,
  output [15:0] out_13,
  output [15:0] out_14,
  output [15:0] out_15,
  output [15:0] out_16,
  output [15:0] out_17
);

  Demultiplexer #(.select(4), .width(16)) demultiplexer_1 (
    .out0(out_2), .out1(out_3), .out2(out_4), .out3(out_5), .out4(out_6), .out5(out_7), .out6(out_8),
    .out7(out_9), .out8(out_10), .out9(out_11), .out10(out_12), .out11(out_13), .out12(out_14),
    .out13(out_15), .out14(out_16), .out15(out_17), .in(in_1[15:0]), .sel(in_1[28:25]));
endmodule

module D (
  input  [28:0] in_1,
  output [28:0] out_2
);

  wire clock_1_out;

  Register #(.width(29)) register_1 (.D(in_1), .en(1'b1), .clk(clock_1_out), .Q(out_2));  // open: clr
  Clock clock_1 (.out(clock_1_out));
endmodule
