// Logisim project ControlUnit.circ as structural Verilog: 2 circuits, main circuit CU
module CU (
  input  [28:0] IR,
  output LoadInstruction
);

  wire [2:0] undriven;
  wire [23:1] rom_1_data;

  CUPC cupc_1 (.pc_out(undriven));  // open: increment, clk, data_in, reset, load, overflow
  ROM #(.addrWidth(9), .dataWidth(24)) rom_1 (.addr({IR[5:0], undriven}), .data({rom_1_data, LoadInstruction}));
endmodule

module CUPC (
  input  reset,
  input  load,
  input  overflow,
  input  increment,
  input  clk,
  input  [2:0] data_in,
  input  [2:0] pc_out
);

  Counter #(.max('h7), .width(3)) counter_1 (
    .clr(reset), .load(load), .up(1'b1), .count(increment), .clk(clk), .D(data_in), .carry(overflow),
    .Q(pc_out));
endmodule
