// Logisim project RegisterFile.circ as structural Verilog: 3 circuits, main circuit RegisterFile16A
module RegisterFile16A (
  input  [3:0] adr_a,
  input  [3:0] adr_b,
  input  write,
  input  [3:0] write_to,
  input  clock,
  input  reset,
  input  [28:0] data,
  output [28:0] a,
  output [28:0] b
);

  wire [3:0] decoder_1_out0, decoder_1_out4, decoder_1_out8, decoder_1_out12;
  wire [28:0] multiplexer_1_out, multiplexer_3_out, multiplexer_4_out, multiplexer_5_out, multiplexer_6_out,
       multiplexer_7_out, multiplexer_9_out, multiplexer_10_out, register_1_q, register_2_q, register_3_q,
       register_4_q, register_5_q, register_6_q, register_7_q, register_8_q, register_9_q, register_10_q,
       register_11_q, register_12_q, register_13_q, register_14_q, register_15_q;

  Decoder #(.select(4)) decoder_1 (
    .out0(decoder_1_out0[0]), .out1(decoder_1_out0[1]), .out2(decoder_1_out0[2]), .out3(decoder_1_out0[3]),
    .out4(decoder_1_out4[0]), .out5(decoder_1_out4[1]), .out6(decoder_1_out4[2]), .out7(decoder_1_out4[3]),
    .out8(decoder_1_out8[0]), .out9(decoder_1_out8[1]), .out10(decoder_1_out8[2]), .out11(decoder_1_out8[3]),
    .out12(decoder_1_out12[0]), .out13(decoder_1_out12[1]), .out14(decoder_1_out12[2]),
    .out15(decoder_1_out12[3]), .sel(write_to), .en(write));
  Register #(.width(29)) register_1 (.D(data), .en(decoder_1_out0[1]), .clk(clock), .Q(register_1_q), .clr(reset));
  Register #(.width(29)) register_2 (.D(data), .en(decoder_1_out0[2]), .clk(clock), .Q(register_2_q), .clr(reset));
  Register #(.width(29)) register_3 (.D(data), .en(decoder_1_out0[3]), .clk(clock), .Q(register_3_q), .clr(reset));
  Multiplexer #(.select(2), .width(29)) multiplexer_1 (
    .in0({29{1'b0}}), .in1(register_1_q), .in2(register_2_q), .in3(register_3_q), .out(multiplexer_1_out),
    .sel(adr_b[1:0]));
  Multiplexer #(.select(2), .width(29)) multiplexer_2 (
    .in0(multiplexer_1_out), .in1(multiplexer_4_out), .in2(multiplexer_6_out), .in3(multiplexer_10_out),
    .out(b), .sel(adr_b[3:2]));
  Multiplexer #(.select(2), .width(29)) multiplexer_3 (
    .in0({29{1'b0}}), .in1(register_1_q), .in2(register_2_q), .in3(register_3_q), .out(multiplexer_3_out),
    .sel(adr_a[1:0]));
  Register #(.width(29)) register_4 (.D(data), .en(decoder_1_out4[0]), .clk(clock), .Q(register_4_q), .clr(reset));
  Register #(.width(29)) register_5 (.D(data), .en(decoder_1_out4[1]), .clk(clock), .Q(register_5_q), .clr(reset));
  Register #(.width(29)) register_6 (.D(data), .en(decoder_1_out4[2]), .clk(clock), .Q(register_6_q), .clr(reset));
  Register #(.width(29)) register_7 (.D(data), .en(decoder_1_out4[3]), .clk(clock), .Q(register_7_q), .clr(reset));
  Multiplexer #(.select(2), .width(29)) multiplexer_4 (
    .in0(register_4_q), .in1(register_5_q), .in2(register_6_q), .in3(register_7_q), .out(multiplexer_4_out),
    .sel(adr_b[1:0]));
  Multiplexer #(.select(2), .width(29)) multiplexer_5 (
    .in0(register_4_q), .in1(register_5_q), .in2(register_6_q), .in3(register_7_q), .out(multiplexer_5_out),
    .sel(adr_a[1:0]));
  Register #(.width(29)) register_8 (.D(data), .en(decoder_1_out8[0]), .clk(clock), .Q(register_8_q), .clr(reset));
  Register #(.width(29)) register_9 (.D(data), .en(decoder_1_out8[1]), .clk(clock), .Q(register_9_q), .clr(reset));
  Register #(.width(29)) register_10 (.D(data), .en(decoder_1_out8[2]), .clk(clock), .Q(register_10_q), .clr(reset));
  Register #(.width(29)) register_11 (.D(data), .en(decoder_1_out8[3]), .clk(clock), .Q(register_11_q), .clr(reset));
  Multiplexer #(.select(2), .width(29)) multiplexer_6 (
    .in0(register_8_q), .in1(register_9_q), .in2(register_10_q), .in3(register_11_q),
    .out(multiplexer_6_out), .sel(adr_b[1:0]));
  Multiplexer #(.select(2), .width(29)) multiplexer_7 (
    .in0(register_8_q), .in1(register_9_q), .in2(register_10_q), .in3(register_11_q),
    .out(multiplexer_7_out), .sel(adr_a[1:0]));
  Register #(.width(29)) register_12 (.D(data), .en(decoder_1_out12[0]), .clk(clock), .Q(register_12_q), .clr(reset));
  Register #(.width(29)) register_13 (.D(data), .en(decoder_1_out12[1]), .clk(clock), .Q(register_13_q), .clr(reset));
  Register #(.width(29)) register_14 (.D(data), .en(decoder_1_out12[2]), .clk(clock), .Q(register_14_q), .clr(reset));
  Register #(.width(29)) register_15 (.D(data), .en(decoder_1_out12[3]), .clk(clock), .Q(register_15_q), .clr(reset));
  Multiplexer #(.select(2), .width(29)) multiplexer_8 (
    .in0(multiplexer_3_out), .in1(multiplexer_5_out), .in2(multiplexer_7_out), .in3(multiplexer_9_out),
    .out(a), .sel(adr_a[3:2]));
  Multiplexer #(.select(2), .width(29)) multiplexer_9 (
    .in0(register_12_q), .in1(register_13_q), .in2(register_14_q), .in3(register_15_q),
    .out(multiplexer_9_out), .sel(adr_a[1:0]));
  Multiplexer #(.select(2), .width(29)) multiplexer_10 (
    .in0(register_12_q), .in1(register_13_q), .in2(register_14_q), .in3(register_15_q),
    .out(multiplexer_10_out), .sel(adr_b[1:0]));
endmodule

module RegisterFile (
  input  [4:0] adr_a,
  input  [4:0] adr_b,
  input  [4:0] write_to,
  input  [28:0] data,
  input  clock,
  input  write,
  input  reset,
  output [28:0] a,
  output [28:0] b
);

  wire demultiplexer_1_out0, demultiplexer_1_out1;
  wire [28:0] registerfile16a_1_a, registerfile16a_1_b, registerfile16b_1_a, registerfile16b_1_b;

  Demultiplexer demultiplexer_1 (
    .out0(demultiplexer_1_out0), .out1(demultiplexer_1_out1), .in(write), .sel(write_to[4]));
  RegisterFile16A registerfile16a_1 (
    .write(demultiplexer_1_out0), .write_to(write_to[3:0]), .clock(clock), .reset(reset), .data(data),
    .adr_a(adr_a[3:0]), .adr_b(adr_b[3:0]), .a(registerfile16a_1_a), .b(registerfile16a_1_b));
  RegisterFile16B registerfile16b_1 (
    .write(demultiplexer_1_out1), .write_to(write_to[3:0]), .clock(clock), .reset(reset), .data(data),
    .adr_a(adr_a[3:0]), .adr_b(adr_b[3:0]), .a(registerfile16b_1_a), .b(registerfile16b_1_b));
  Multiplexer #(.disabled("Z"), .width(29)) multiplexer_1 (
    .in0(registerfile16a_1_a), .in1(registerfile16b_1_a), .out(a), .sel(adr_a[4]));
  Multiplexer #(.disabled("Z"), .width(29)) multiplexer_2 (
    .in0(registerfile16a_1_b), .in1(registerfile16b_1_b), .out(b), .sel(adr_b[4]));
endmodule

module RegisterFile16B (
  input  [3:0] adr_a,
  input  [3:0] adr_b,
  input  write,
  input  [3:0] write_to,
  input  clock,
  input  reset,
  input  [28:0] data,
  output [28:0] a,
  output [28:0] b
);

  wire [3:0] decoder_1_out0, decoder_1_out4, decoder_1_out8, decoder_1_out12;
  wire [28:0] multiplexer_1_out, multiplexer_3_out, multiplexer_4_out, multiplexer_5_out, multiplexer_6_out,
       multiplexer_7_out, multiplexer_9_out, multiplexer_10_out, random_1_out, register_1_q, register_2_q,
       register_3_q, register_4_q, register_5_q, register_6_q, register_7_q, register_8_q, register_9_q,
       register_10_q, register_11_q, register_12_q, register_13_q, register_14_q, register_15_q;

  Decoder #(.select(4)) decoder_1 (
    .out0(decoder_1_out0[0]), .out1(decoder_1_out0[1]), .out2(decoder_1_out0[2]), .out3(decoder_1_out0[3]),
    .out4(decoder_1_out4[0]), .out5(decoder_1_out4[1]), .out6(decoder_1_out4[2]), .out7(decoder_1_out4[3]),
    .out8(decoder_1_out8[0]), .out9(decoder_1_out8[1]), .out10(decoder_1_out8[2]), .out11(decoder_1_out8[3]),
    .out12(decoder_1_out12[0]), .out13(decoder_1_out12[1]), .out14(decoder_1_out12[2]),
    .out15(decoder_1_out12[3]), .sel(write_to), .en(write));
  Random #(.width(29)) random_1 (.clr(reset), .next(1'b1), .clk(clock), .out(random_1_out));
  Register #(.width(29)) register_1 (.D(data), .en(decoder_1_out0[1]), .clk(clock), .Q(register_1_q), .clr(reset));
  Register #(.width(29)) register_2 (.D(data), .en(decoder_1_out0[2]), .clk(clock), .Q(register_2_q), .clr(reset));
  Register #(.width(29)) register_3 (.D(data), .en(decoder_1_out0[3]), .clk(clock), .Q(register_3_q), .clr(reset));
  Multiplexer #(.select(2), .width(29)) multiplexer_1 (
    .in0(random_1_out), .in1(register_1_q), .in2(register_2_q), .in3(register_3_q), .out(multiplexer_1_out),
    .sel(adr_b[1:0]));
  Multiplexer #(.select(2), .width(29)) multiplexer_2 (
    .in0(multiplexer_1_out), .in1(multiplexer_4_out), .in2(multiplexer_6_out), .in3(multiplexer_10_out),
    .out(b), .sel(adr_b[3:2]));
  Multiplexer #(.select(2), .width(29)) multiplexer_3 (
    .in0(random_1_out), .in1(register_1_q), .in2(register_2_q), .in3(register_3_q), .out(multiplexer_3_out),
    .sel(adr_a[1:0]));
  Register #(.width(29)) register_4 (.D(data), .en(decoder_1_out4[0]), .clk(clock), .Q(register_4_q), .clr(reset));
  Register #(.width(29)) register_5 (.D(data), .en(decoder_1_out4[1]), .clk(clock), .Q(register_5_q), .clr(reset));
  Register #(.width(29)) register_6 (.D(data), .en(decoder_1_out4[2]), .clk(clock), .Q(register_6_q), .clr(reset));
  Register #(.width(29)) register_7 (.D(data), .en(decoder_1_out4[3]), .clk(clock), .Q(register_7_q), .clr(reset));
  Multiplexer #(.select(2), .width(29)) multiplexer_4 (
    .in0(register_4_q), .in1(register_5_q), .in2(register_6_q), .in3(register_7_q), .out(multiplexer_4_out),
    .sel(adr_b[1:0]));
  Multiplexer #(.select(2), .width(29)) multiplexer_5 (
    .in0(register_4_q), .in1(register_5_q), .in2(register_6_q), .in3(register_7_q), .out(multiplexer_5_out),
    .sel(adr_a[1:0]));
  Register #(.width(29)) register_8 (.D(data), .en(decoder_1_out8[0]), .clk(clock), .Q(register_8_q), .clr(reset));
  Register #(.width(29)) register_9 (.D(data), .en(decoder_1_out8[1]), .clk(clock), .Q(register_9_q), .clr(reset));
  Register #(.width(29)) register_10 (.D(data), .en(decoder_1_out8[2]), .clk(clock), .Q(register_10_q), .clr(reset));
  Register #(.width(29)) register_11 (.D(data), .en(decoder_1_out8[3]), .clk(clock), .Q(register_11_q), .clr(reset));
  Multiplexer #(.select(2), .width(29)) multiplexer_6 (
    .in0(register_8_q), .in1(register_9_q), .in2(register_10_q), .in3(register_11_q),
    .out(multiplexer_6_out), .sel(adr_b[1:0]));
  Multiplexer #(.select(2), .width(29)) multiplexer_7 (
    .in0(register_8_q), .in1(register_9_q), .in2(register_10_q), .in3(register_11_q),
    .out(multiplexer_7_out), .sel(adr_a[1:0]));
  Register #(.width(29)) register_12 (.D(data), .en(decoder_1_out12[0]), .clk(clock), .Q(register_12_q), .clr(reset));
  Register #(.width(29)) register_13 (.D(data), .en(decoder_1_out12[1]), .clk(clock), .Q(register_13_q), .clr(reset));
  Register #(.width(29)) register_14 (.D(data), .en(decoder_1_out12[2]), .clk(clock), .Q(register_14_q), .clr(reset));
  Register #(.width(29)) register_15 (.D(data), .en(decoder_1_out12[3]), .clk(clock), .Q(register_15_q), .clr(reset));
  Multiplexer #(.select(2), .width(29)) multiplexer_8 (
    .in0(multiplexer_3_out), .in1(multiplexer_5_out), .in2(multiplexer_7_out), .in3(multiplexer_9_out),
    .out(a), .sel(adr_a[3:2]));
  Multiplexer #(.select(2), .width(29)) multiplexer_9 (
    .in0(register_12_q), .in1(register_13_q), .in2(register_14_q), .in3(register_15_q),
    .out(multiplexer_9_out), .sel(adr_a[1:0]));
  Multiplexer #(.select(2), .width(29)) multiplexer_10 (
    .in0(register_12_q), .in1(register_13_q), .in2(register_14_q), .in3(register_15_q),
    .out(multiplexer_10_out), .sel(adr_b[1:0]));
endmodule
