// Logisim project cache.circ as structural Verilog: 3 circuits, main circuit cache
module cache (
  input  [4:0] mar,
  input  [28:0] im_mbr,
  input  clk,
  input  rst,
  input  mbrem,
  input  load_i,
  input  rw,
  input  en,
  input  [28:0] ram_data,
  input  [4:0] ram_addr,
  output [28:0] data_out,
  output [28:0] ram_in,
  output rread,
  output rwrite
);

  wire aa4_1_out_3, aa4_2_out_3, aa4_3_out_3, aa4_4_out_3, aa4_5_out_3, aa4_6_out_3, aa4_7_out_3,
       aa4_8_out_3, aa4_9_out_3, aa4_10_out_3, aa4_11_out_3, cpy, cpy_done, hit, mbre, multiplexer_1_out,
       not_1_out, or_1_out, or_2_out, pause, read, t, wcpy, write;
  wire [1:0] cache_mar;
  wire [3:0] pc, pcload;
  wire [28:0] data, multiplexer_5_out;
  wire [31:0] b;

  ROM #(.addrWidth(4)) rom_1 (.addr(pc), .data({read, write, cpy, rread, rwrite, mbre, wcpy, pause}));
  RAM #(.addrWidth(3), .asyncread("true"), .dataWidth(32)) ram_1 (
    .addr({mar[2], cache_mar}), .we(write), .oe(read), .clk(clk), .din({mar[4:3], 1'b1, data}), .dout(b));
  // Probe on data_out
  D_Flip_Flop #(.trigger("falling")) d_ff_1 (.D(multiplexer_1_out), .clk(clk), .Q(t));  // open: Qn, preset, reset
  Multiplexer multiplexer_1 (.in0(pause), .in1(1'b1), .out(multiplexer_1_out));  // open: sel
  Register #(.width(4)) register_1 (.D(pcload), .en(t), .clk(clk), .Q(pc), .clr(rst));
  Counter #(.max('h3), .width(2)) counter_1 (
    .clr(rst), .load(1'b0), .up(1'b1), .count(wcpy), .clk(clk), .carry(cpy_done), .Q(ram_addr[1:0]));  // open: D
  AA4 aa4_1 (.in_1(pc), .in_2(4'b0000), .out_3(aa4_1_out_3));
  Multiplexer #(.disabled("Z"), .enable("true"), .width(4)) multiplexer_2 (
    .in0(4'b0001), .in1(4'b0001), .out(pcload), .sel(1'b1), .en(aa4_1_out_3));
  AA4 aa4_2 (.in_1(pc), .in_2(4'b0100), .out_3(aa4_2_out_3));
  Multiplexer #(.disabled("Z"), .enable("true"), .width(4)) multiplexer_3 (
    .in0(4'b0101), .in1(4'b0101), .out(pcload), .sel(1'b1), .en(aa4_2_out_3));
  AA4 aa4_3 (.in_1(pc), .in_2(4'b0111), .out_3(aa4_3_out_3));
  Multiplexer #(.disabled("Z"), .enable("true"), .width(4)) multiplexer_4 (
    .in0(4'b1000), .in1(4'b0010), .out(pcload), .sel(1'b0), .en(aa4_3_out_3));
  Multiplexer #(.width(29)) multiplexer_5 (.in0(b[28:0]), .in1(im_mbr), .out(multiplexer_5_out));  // open: sel
  Multiplexer #(.width(29)) multiplexer_6 (.in0(data_out), .in1(ram_data), .out(data), .sel(cpy));
  Comparator #(.mode("unsigned"), .width(2)) comparator_1 (.a(mar[4:3]), .b(ram_addr[4:3]), .eq(hit));  // open: gt, lt
  Multiplexer #(.width(2)) multiplexer_7 (.in0(mar[1:0]), .in1(ram_addr[1:0]), .out(cache_mar), .sel(cpy));
  Register #(.trigger("falling"), .width(29)) register_2 (.D(b[28:0]), .en(1'b1), .clk(clk), .Q(ram_in), .clr(rst));
  Multiplexer #(.width(2)) multiplexer_8 (.in0(b[31:30]), .in1(mar[4:3]), .out(ram_addr[4:3]), .sel(not_1_out));
  not not_1 (not_1_out, read);
  Register #(.width(29)) mbr (.D(multiplexer_5_out), .en(or_1_out), .clk(or_2_out), .Q(data_out), .clr(rst));
  or or_1 (or_1_out, mbre, mbrem);
  or or_2 (or_2_out, mbrem, clk);
  AA4 aa4_4 (.in_1(pc), .in_2(4'b0001), .out_3(aa4_4_out_3));
  Multiplexer #(.disabled("Z"), .enable("true"), .width(4)) multiplexer_9 (
    .in0(4'b0010), .in1(4'b0110), .out(pcload), .sel(b[29]), .en(aa4_4_out_3));
  AA4 aa4_5 (.in_1(pc), .in_2(4'b0100), .out_3(aa4_5_out_3));
  Multiplexer #(.disabled("Z"), .enable("true"), .width(4)) multiplexer_10 (
    .in0(4'b0100), .in1(4'b0101), .out(pcload), .sel(mbre), .en(aa4_5_out_3));
  AA4 aa4_6 (.in_1(pc), .in_2(4'b1000), .out_3(aa4_6_out_3));
  Multiplexer #(.disabled("Z"), .enable("true"), .width(4)) multiplexer_11 (
    .in0(4'b0110), .in1(4'b0010), .out(pcload), .sel(cpy_done), .en(aa4_6_out_3));
  AA4 aa4_7 (.in_1(pc), .in_2(4'b0010), .out_3(aa4_7_out_3));
  Multiplexer #(.disabled("Z"), .enable("true"), .width(4)) multiplexer_12 (
    .in0(4'b0010), .in1(4'b0011), .out(pcload), .sel(cpy_done), .en(aa4_7_out_3));
  AA4 aa4_8 (.in_1(pc), .in_2(4'b0101), .out_3(aa4_8_out_3));
  Multiplexer #(.disabled("Z"), .enable("true"), .width(4)) multiplexer_13 (
    .in0(4'b0000), .in1(4'b0000), .out(pcload), .sel(1'b1), .en(aa4_8_out_3));
  AA4 aa4_9 (.in_1(pc), .in_2(4'b1001), .out_3(aa4_9_out_3));
  Multiplexer #(.disabled("Z"), .enable("true"), .width(4)) multiplexer_14 (
    .in0(4'b0000), .in1(4'b0000), .out(pcload), .sel(mbre), .en(aa4_9_out_3));
  AA4 aa4_10 (.in_1(pc), .in_2(4'b0011), .out_3(aa4_10_out_3));
  Multiplexer #(.disabled("Z"), .enable("true"), .width(4)) multiplexer_15 (
    .in0(4'b0100), .in1(4'b1001), .out(pcload), .sel(rw), .en(aa4_10_out_3));
  AA4 aa4_11 (.in_1(pc), .in_2(4'b0110), .out_3(aa4_11_out_3));
  Multiplexer #(.disabled("Z"), .enable("true"), .width(4)) multiplexer_16 (
    .in0(4'b0111), .in1(4'b0011), .out(pcload), .sel(hit), .en(aa4_11_out_3));

  assign ram_addr[2] = mar[2];

  // Other names for the same wires on the sheet: a[28:0] = ram_in; cache_data[28:0] = b[28:0]; has_data = b[29];
  //   curr_block_addr[1:0] = mar[4:3]; mbr[28:0] = data_out; c_offset[1:0] = ram_addr[1:0]; cache_mar[2] = mar[2];
  //   block_addr[1:0] = ram_addr[4:3]

  // Notes on the sheet:
  //   contents of rom_1 (hex, n*v repeats v):
  //   90 81 73 91 95 a1 a1 1 ab 45
endmodule

module AA4 (
  input  [3:0] in_1,
  input  [3:0] in_2,
  output out_3
);

  Comparator #(.width(4)) comparator_1 (.a(in_1), .b(in_2), .eq(out_3));  // open: gt, lt
endmodule

module cache_testbench (
);

  cache cache_1 ();  // open: mar, im_mbr, clk, rst, mbrem, load_i, rw, en, ram_data, ram_addr, data_out, ram_in, rread, rwrite
endmodule
