// Logisim project cache AIO.circ as structural Verilog
module main (
  input  [4:0] in_1,
  input  [28:0] in_2,
  input  in_3,
  input  in_4,
  input  [7:0] in_5,
  input  in_6
);

  wire aa4_1_out_3, aa4_2_out_3, aa4_3_out_3, aa4_4_out_3, aa4_5_out_3, aa4_6_out_3, aa4_7_out_3,
       aa4_8_out_3, aa4_9_out_3, aa4_10_out_3, aa4_11_out_3, clk, clock_1_out, clock_3_out, clock_4_out,
       clock_5_out, clock_6_out, clock_7_out, clock_8_out, cpy, cpy_done, hit, mbre, mbrem,
       multiplexer_1_out, not_1_out, or_1_out, or_2_out, pause, read, rread, rst, rwrite, t, wcpy, write;
  wire [1:0] block_addr, c_offset, cache_mar;
  wire [3:0] pc, pcload;
  wire [28:0] a, data, mbr, multiplexer_5_out, ram_data;
  wire [31:0] b;

  ROM #(.addrWidth(4)) rom_1 (.addr(pc), .data({read, write, cpy, rread, rwrite, mbre, wcpy, pause}));
  Clock clock_1 (.out(clock_1_out));
  RAM #(.addrWidth(3), .dataWidth(32)) ram_1 (
    .addr({in_1[2], cache_mar}), .we(write), .oe(read), .clk(clock_1_out), .din({in_1[4:3], 1'b1, data}),
    .dout(b));
  Clock clock_2 (.out(clk));
  Button button_1 (.out(rst));
  Clock clock_3 (.out(clock_3_out));
  Clock clock_4 (.out(clock_4_out));
  // Probe on mbr
  D_Flip_Flop #(.trigger("falling")) d_ff_1 (
    .D(multiplexer_1_out), .clk(clock_3_out), .Q(t));  // open: Qn, preset, reset
  Multiplexer multiplexer_1 (.in0(pause), .in1(1'b1), .out(multiplexer_1_out));  // open: sel
  Register #(.width(4)) register_1 (.D(pcload), .en(t), .clk(clock_4_out), .Q(pc), .clr(rst));
  Clock clock_5 (.out(clock_5_out));
  Counter #(.max('h3), .width(2)) counter_1 (
    .clr(rst), .load(1'b0), .up(1'b1), .count(wcpy), .clk(clock_6_out), .carry(cpy_done), .Q(c_offset));  // open: D
  Clock clock_6 (.out(clock_6_out));
  RAM #(.addrWidth(5), .dataWidth(29), .trigger("falling"), .\type ("nonvolatile")) ram_2 (
    .addr({block_addr, in_1[2], c_offset}), .we(rwrite), .oe(rread), .clk(clock_5_out), .din(a),
    .dout(ram_data));
  Button button_2 (.out(mbrem));
  Clock clock_7 (.out(clock_7_out));
  AA4 aa4_1 (.in_1(pc), .in_2(4'b0000), .out_3(aa4_1_out_3));
  Multiplexer #(.disabled("Z"), .enable("true"), .width(4)) multiplexer_2 (
    .in0(4'b0001), .in1(4'b0001), .out(pcload), .sel(1'b1), .en(aa4_1_out_3));
  AA4 aa4_2 (.in_1(pc), .in_2(4'b0100), .out_3(aa4_2_out_3));
  Multiplexer #(.disabled("Z"), .enable("true"), .width(4)) multiplexer_3 (
    .in0(4'b0101), .in1(4'b0101), .out(pcload), .sel(1'b1), .en(aa4_2_out_3));
  AA4 aa4_3 (.in_1(pc), .in_2(4'b0111), .out_3(aa4_3_out_3));
  Multiplexer #(.disabled("Z"), .enable("true"), .width(4)) multiplexer_4 (
    .in0(4'b1000), .in1(4'b0010), .out(pcload), .sel(1'b0), .en(aa4_3_out_3));
  // Probe on in_5
  Multiplexer #(.width(29)) multiplexer_5 (.in0(b[28:0]), .in1(in_2), .out(multiplexer_5_out));  // open: sel
  Multiplexer #(.width(29)) multiplexer_6 (.in0(mbr), .in1(ram_data), .out(data), .sel(cpy));
  Comparator #(.mode("unsigned"), .width(2)) comparator_1 (.a(in_1[4:3]), .b(block_addr), .eq(hit));  // open: gt, lt
  Multiplexer #(.width(2)) multiplexer_7 (.in0(in_1[1:0]), .in1(c_offset), .out(cache_mar), .sel(cpy));
  Register #(.trigger("falling"), .width(29)) register_2 (.D(b[28:0]), .en(1'b1), .clk(clock_8_out), .Q(a), .clr(rst));
  Clock clock_8 (.out(clock_8_out));
  Multiplexer #(.width(2)) multiplexer_8 (.in0(b[31:30]), .in1(in_1[4:3]), .out(block_addr), .sel(not_1_out));
  not not_1 (not_1_out, read);
  Register #(.width(29)) u_mbr (.D(multiplexer_5_out), .en(or_1_out), .clk(or_2_out), .Q(mbr), .clr(rst));
  or or_1 (or_1_out, mbre, mbrem);
  or or_2 (or_2_out, mbrem, clock_7_out);
  AA4 aa4_4 (.in_1(pc), .in_2(4'b0001), .out_3(aa4_4_out_3));
  Multiplexer #(.disabled("Z"), .enable("true"), .width(4)) multiplexer_9 (
    .in0(4'b0010), .in1(4'b0110), .out(pcload), .sel(b[29]), .en(aa4_4_out_3));
  AA4 aa4_5 (.in_1(pc), .in_2(4'b0100), .out_3(aa4_5_out_3));
  Multiplexer #(.disabled("Z"), .enable("true"), .width(4)) multiplexer_10 (
    .in0(4'b0100), .in1(4'b0101), .out(pcload), .sel(mbre), .en(aa4_5_out_3));
  AA4 aa4_6 (.in_1(pc), .in_2(4'b1000), .out_3(aa4_6_out_3));
  Multiplexer #(.disabled("Z"), .enable("true"), .width(4)) multiplexer_11 (
    .in0(4'b0110), .in1(4'b0010), .out(pcload), .sel(cpy_done), .en(aa4_6_out_3));
  AA4 aa4_7 (.in_1(pc), .in_2(4'b0010), .out_3(aa4_7_out_3));
  Multiplexer #(.disabled("Z"), .enable("true"), .width(4)) multiplexer_12 (
    .in0(4'b0010), .in1(4'b0011), .out(pcload), .sel(cpy_done), .en(aa4_7_out_3));
  AA4 aa4_8 (.in_1(pc), .in_2(4'b0101), .out_3(aa4_8_out_3));
  Multiplexer #(.disabled("Z"), .enable("true"), .width(4)) multiplexer_13 (
    .in0(4'b0000), .in1(4'b0000), .out(pcload), .sel(1'b1), .en(aa4_8_out_3));
  AA4 aa4_9 (.in_1(pc), .in_2(4'b1001), .out_3(aa4_9_out_3));
  Multiplexer #(.disabled("Z"), .enable("true"), .width(4)) multiplexer_14 (
    .in0(4'b0000), .in1(4'b0000), .out(pcload), .sel(mbre), .en(aa4_9_out_3));
  AA4 aa4_10 (.in_1(pc), .in_2(4'b0011), .out_3(aa4_10_out_3));
  Multiplexer #(.disabled("Z"), .enable("true"), .width(4)) multiplexer_15 (
    .in0(4'b0100), .in1(4'b1001), .out(pcload), .sel(in_3), .en(aa4_10_out_3));
  AA4 aa4_11 (.in_1(pc), .in_2(4'b0110), .out_3(aa4_11_out_3));
  Multiplexer #(.disabled("Z"), .enable("true"), .width(4)) multiplexer_16 (
    .in0(4'b0111), .in1(4'b0011), .out(pcload), .sel(hit), .en(aa4_11_out_3));

  // Other names for the same wires on the sheet: cache_mar[2] = in_1[2]; mar[4:0] = in_1; cache_data[28:0] = b[28:0];
  //   has_data = b[29]; im_mbr[28:0] = in_2; load_i = in_4; curr_block_addr[1:0] = in_1[4:3]; rw = in_3

  // Notes on the sheet:
  //   contents of rom_1 (hex, n*v repeats v):
  //   90 81 73 91 95 a1 a1 1 ab 45
endmodule

module AA4 (
  input  [3:0] in_1,
  input  [3:0] in_2,
  output out_3
);

  Comparator #(.width(4)) comparator_1 (.a(in_1), .b(in_2), .eq(out_3));  // open: gt, lt
endmodule
